# Fritzing sketch Schaltplan_Arduino_Temperatur_mit_WIFI (saved by Fritzing 0.9.9b)
circuit board: 8.46667cm x 5.64444cm
breadboards: 1

parts:
  part = Arduino Uno (Rev3)
  DHT11_-_temperatur_sensor = DHT11 Humitidy and Temperature Sensor (3 pins)
  WIFI_WLAN = ESP8266 ESP-01 Upgraded WiFi Module [part_number=ESP8266]

nets:
  N1: part.D8, DHT11_-_temperatur_sensor.DATA
  GND: part.GND, DHT11_-_temperatur_sensor.GND, WIFI_WLAN.GND
  N2: part.D2, WIFI_WLAN.TXD
  N3: part.D3_PWM, WIFI_WLAN.RXD
  3V3: part.3V3, WIFI_WLAN.VCC, WIFI_WLAN.CH_PD
  5V: part.5V, DHT11_-_temperatur_sensor.VDD

custom parts:
  DHT11 Humitidy and Temperature Sensor (3 pins): DHT11 Humidity and Temperature Sensor (3 pins) from the design created by John De Cristofaro for Adafruit Industries.
  ESP8266 ESP-01 Upgraded WiFi Module: Upgraded Version ESP-01,all Flash are upgraded to 1M byte.Also support Cloud service remote transmission.
